# Fritzing sketch Kiki_Desktop (saved by Fritzing 1.0.1)

parts:
  U1_Raspberry_Pi_5 = U1 Raspberry Pi 5
  BT1_USB_power_bank = BT1 USB power bank
  DS1_SSD1306_OLED = DS1 SSD1306 OLED
  DS2_16_x_2_LCD = DS2 16 x 2 LCD
  S1_LEFT_infrared_sensor = S1 LEFT infrared sensor
  S2_RIGHT_infrared_sensor = S2 RIGHT infrared sensor
  U2_Hailo_AI_HAT+_2 = U2 Hailo AI HAT+ 2
  CAM1_USB_webcam = CAM1 USB webcam
  U3_ULN2003_driver = U3 ULN2003 driver
  M1_28BYJ-48 = M1 28BYJ-48
  LS1_Bluetooth_speaker = LS1 Bluetooth speaker  # not connected

nets:
  N1: U1_Raspberry_Pi_5.USB-C_/_POWER, BT1_USB_power_bank.USB-C_power_cable
  N2: U1_Raspberry_Pi_5.3V3_/_physical_1, DS1_SSD1306_OLED.VCC_/_3.3V, DS2_16_x_2_LCD.3V3_/_LV_reference, S1_LEFT_infrared_sensor.VCC_/_3.3V_compatible, S2_RIGHT_infrared_sensor.VCC_/_3.3V_compatible
  GND: U1_Raspberry_Pi_5.GND_/_physical_6, DS1_SSD1306_OLED.GND, DS2_16_x_2_LCD.GND, S1_LEFT_infrared_sensor.GND, S2_RIGHT_infrared_sensor.GND, U3_ULN2003_driver.GND
  N3: U1_Raspberry_Pi_5.GPIO2_SDA_/_physical_3, DS1_SSD1306_OLED.SDA, DS2_16_x_2_LCD.SDA_/_LV_side
  N4: U1_Raspberry_Pi_5.GPIO3_SCL_/_physical_5, DS1_SSD1306_OLED.SCL, DS2_16_x_2_LCD.SCL_/_LV_side
  N5: U1_Raspberry_Pi_5.5V_/_physical_2, U1_Raspberry_Pi_5.5V_/_physical_4, DS2_16_x_2_LCD.5V_supply, U3_ULN2003_driver.V+_/_5V
  N6: U1_Raspberry_Pi_5.GPIO22_/_physical_15, S1_LEFT_infrared_sensor.OUT
  N7: U1_Raspberry_Pi_5.GPIO17_/_physical_11, S2_RIGHT_infrared_sensor.OUT
  N8: U1_Raspberry_Pi_5.PCIe_/_accelerator_link, U2_Hailo_AI_HAT+_2.PCIe_FFC_cable
  N9: U1_Raspberry_Pi_5.HAT_header_/_power_+_ID, U2_Hailo_AI_HAT+_2.40-pin_stacking_header
  N10: U1_Raspberry_Pi_5.USB_host_/_camera, CAM1_USB_webcam.USB_cable
  N11: U1_Raspberry_Pi_5.GPIO21_/_physical_40, U3_ULN2003_driver.IN1
  N12: U1_Raspberry_Pi_5.GPIO16_/_physical_36, U3_ULN2003_driver.IN2
  N13: U1_Raspberry_Pi_5.GPIO12_/_physical_32, U3_ULN2003_driver.IN3
  N14: U1_Raspberry_Pi_5.GPIO26_/_physical_37, U3_ULN2003_driver.IN4
  N15: U3_ULN2003_driver.Motor_/_5-wire_harness, M1_28BYJ-48.5-pin_motor_plug

custom parts:
  U1 Raspberry Pi 5: Desktop module wiring reference. Cable ports represent complete cables. No PCB footprint.
  BT1 USB power bank: Desktop module wiring reference. Cable ports represent complete cables. No PCB footprint.
  DS1 SSD1306 OLED: Desktop module wiring reference. Cable ports represent complete cables. No PCB footprint.
  DS2 16 x 2 LCD: Desktop module wiring reference. Cable ports represent complete cables. No PCB footprint.
  S1 LEFT infrared sensor: Desktop module wiring reference. Cable ports represent complete cables. No PCB footprint.
  S2 RIGHT infrared sensor: Desktop module wiring reference. Cable ports represent complete cables. No PCB footprint.
  U2 Hailo AI HAT+ 2: Desktop module wiring reference. Cable ports represent complete cables. No PCB footprint.
  CAM1 USB webcam: Desktop module wiring reference. Cable ports represent complete cables. No PCB footprint.
  U3 ULN2003 driver: Desktop module wiring reference. Cable ports represent complete cables. No PCB footprint.
  M1 28BYJ-48: Desktop module wiring reference. Cable ports represent complete cables. No PCB footprint.
  LS1 Bluetooth speaker: Desktop module wiring reference. Cable ports represent complete cables. No PCB footprint.
