# Fritzing sketch Kiki_Wearable (saved by Fritzing 1.0.1)

parts:
  U1 = Waveshare ESP32-S3 Touch AMOLED 1.75 (cased)
  U2 = MAX30102 breakout (4 used connections)
  BT1 = Li-Po 1S 3.7V 1000mAh
  LS1 = DFRobot FIT0502 8 ohm 3W

nets:
  N1: U1.3V3_[H2/3], U2.VIN
  N2: U1.GND_[H2/2], U1.BAT-, U2.GND, BT1.-
  N3: U1.GPIO18_/_SDA_[H2/7], U2.SDA
  N4: U1.GPIO17_/_SCL_[H2/6], U2.SCL
  N5: U1.BAT+, BT1.+
  N6: U1.SPK+, LS1.+
  N7: U1.SPK-, LS1.-

custom parts:
  Waveshare ESP32-S3 Touch AMOLED 1.75 (cased): Custom wiring-reference part. Breadboard placement is illustrative; no manufacturing PCB footprint. Use connector labels and verify physical polarity.
  MAX30102 breakout (4 used connections): Custom wiring-reference part. Breadboard placement is illustrative; no manufacturing PCB footprint. Use connector labels and verify physical polarity.
  Li-Po 1S 3.7V 1000mAh: Custom wiring-reference part. Breadboard placement is illustrative; no manufacturing PCB footprint. Use connector labels and verify physical polarity.
  DFRobot FIT0502 8 ohm 3W: Custom wiring-reference part. Breadboard placement is illustrative; no manufacturing PCB footprint. Use connector labels and verify physical polarity.
